# Fritzing sketch NRF24L01_AVR328P_board (saved by Fritzing 0.9.2b)
breadboards: 1

parts:
  U1 = atmega328 [package=dip]
  C2 = Ceramic Capacitor [capacitance=100nF package="100 mil [THT, multilayer]"]
  Q1 = TRANSISTOR_NPN [package=to-92]
  FTDI = female pin header, 4 pins [form="♀ (female)"]
  ICP = mystery part, 6 pins [chip_label="ICP Header"]
  U2 = TEMPERATURE-SENSOR [package=to-92]
  R1 = Resistor [tolerance=±5% resistance=4.7k package=THT]
  Moisture = male pin header, 3 pins [form="♂ (male)"]
  J1 = female pin header, 8 pins [form="♀ (female)"]

nets:
  N1: U1.RESET, U1.GND#7, C2.1, Q1.E, Q1.B, FTDI.pin4, ICP.pin3, ICP.pin4
  N2: U1.D0_(RX), FTDI.pin2
  N3: U1.D1_(TX), FTDI.pin1
  N4: U1.D2, J1.pin2
  N5: U1.VCC, U1.D12, C2.0, ICP.pin1, ICP.pin6, J1.pin3
  N6: U1.D9_(PWM), J1.pin7
  N7: U1.D10_(PWM), J1.pin6
  N8: U1.D11_(PWM), U1.D13, ICP.pin2, ICP.pin5, J1.pin4, J1.pin5
  N9: U1.A0, U2.ADJ, R1.Pin_0
  N10: U1.A1, Moisture.pin1
  N11: Q1.C, U2.GND, Moisture.pin2, J1.pin1
  N12: U2.VCC, R1.Pin_1, Moisture.pin3, J1.pin8
