# Fritzing sketch NRF24L01_AVR328P_stripboard (saved by Fritzing 0.9.2b)
stripboards: 1

parts:
  ICP = mystery part, 6 pins [chip_label="ICP Header"]
  Moisture = male pin header, 3 pins [form="♂ (male)"]
  U3 = atmega328 [package=dip]
  C3 = Ceramic Capacitor [capacitance=100nF package="100 mil [THT, multilayer]"]
  Radio = female pin header, 8 pins [form="♀ (female)"]
  Gnd_Disconnect = NPN-Transistor [package="TO92 [THT]"]
  Temperature = TEMPERATURE-SENSOR [package=to-92]
  R2 = Resistor [tolerance=±5% resistance=4.7k package=THT]
  J1 = Screw terminal - 2 pins [package=THT]
  D1 = Rectifier Diode [part_number=1N4001 package="300 mil [THT]"]
  FTDI = male pin header, 6 pins [form="♂ (male)"]
  CE_PD = Resistor [tolerance=±5% resistance=1.2M package=THT]
  CSN_PU = Resistor [tolerance=±5% resistance=12k package=THT]

nets:
  N1: ICP.pin1, U3.D12, Radio.pin3
  N2: ICP.pin2, U3.D13, Radio.pin5
  N3: ICP.pin3, U3.RESET, Gnd_Disconnect.B
  N4: ICP.pin4, Radio.pin1, Gnd_Disconnect.E, J1.pin2, FTDI.pin6, CE_PD.Pin_1
  N5: ICP.pin5, U3.D11_(PWM), Radio.pin4
  VCC: ICP.pin6, Moisture.pin3, U3.VCC, U3.AVCC, C3.1, Radio.pin8, Temperature.VCC, R2.Pin_1, J1.pin1, D1.cathode, CSN_PU.Pin_1
  N6: Moisture.pin1, U3.A1
  N7: Moisture.pin2, Gnd_Disconnect.C, Temperature.GND
  N8: U3.D0_(RX), FTDI.pin3
  N9: U3.D1_(TX), FTDI.pin2
  N10: U3.D2, Radio.pin2
  N11: U3.GND#7, C3.0
  N12: U3.D9_(PWM), Radio.pin7, CE_PD.Pin_0
  N13: U3.D10_(PWM), Radio.pin6, CSN_PU.Pin_0
  N14: U3.A0, Temperature.ADJ, R2.Pin_0
  N15: D1.anode, FTDI.pin4
